# Fritzing sketch robot (saved by Fritzing 0.9.3b)
circuit board: 19.2841cm x 12.0651cm
breadboards: 1

parts:
  SERVO1_RIGHT = Basic Servo
  SERVO2_LEFT = Basic Servo
  LDR2_RIGHT = Photocell (LDR) [package=THT]
  POT_LEFT = POT [package=3362u]
  SPKR1 = Loudspeaker
  SERVO3_HEAD = Basic Servo
  PWM_16_CHANNEL_25_mA_max = Adafruit PCA9685 PWM/Servo Breakout [part_number=PCA9685]
  HCSR04 = HC-SR04 Ultrasonic Distance Sensor
  LDR1_LEFT = Photocell (LDR) [package=THT]
  LIPO_5V_1A = Battery Holders [package=lipo-1100mAh]
  RGB_LED1 = RGB LED (com. cathode, rgb) [package="5 mm [THT]"]
  ARDUINO_MICRO = Arduino Micro (Rev3)
  POT_RIGHT = POT [package=3362u]
  BUTTON = Round Pushbutton

nets:
  GND: SERVO1_RIGHT.gnd, SERVO2_LEFT.gnd, POT_LEFT.A, SPKR1.pin2, SERVO3_HEAD.gnd, PWM_16_CHANNEL_25_mA_max.GND, HCSR04.GND, LIPO_5V_1A.-, RGB_LED1.common_cathode, ARDUINO_MICRO.GND, POT_RIGHT.A
  VCC: SERVO1_RIGHT.vcc, SERVO2_LEFT.vcc, SERVO3_HEAD.vcc, PWM_16_CHANNEL_25_mA_max.5.0V
  N1: SERVO1_RIGHT.pulse, PWM_16_CHANNEL_25_mA_max.PWM1
  N2: SERVO2_LEFT.pulse, PWM_16_CHANNEL_25_mA_max.PWM2
  N3: LDR2_RIGHT.pin_0, POT_RIGHT.E
  VCC_2: LDR2_RIGHT.pin_1, PWM_16_CHANNEL_25_mA_max.VCC, HCSR04.VCC, LDR1_LEFT.pin_1, ARDUINO_MICRO.5V
  N4: POT_LEFT.E, LDR1_LEFT.pin_0
  N5: POT_LEFT.S, ARDUINO_MICRO.A4
  N6: SPKR1.pin1, ARDUINO_MICRO.D5_PWM
  N7: SERVO3_HEAD.pulse, PWM_16_CHANNEL_25_mA_max.PWM3
  N8: PWM_16_CHANNEL_25_mA_max.PWRIN, BUTTON.leg0
  N9: PWM_16_CHANNEL_25_mA_max.SDA, ARDUINO_MICRO.D2/SDA
  N10: PWM_16_CHANNEL_25_mA_max.SCL, ARDUINO_MICRO.D3/SCL
  N11: PWM_16_CHANNEL_25_mA_max.PWM15, RGB_LED1.red_anode
  N12: PWM_16_CHANNEL_25_mA_max.PWM14, RGB_LED1.green_anode
  N13: PWM_16_CHANNEL_25_mA_max.PWM13, RGB_LED1.blue_anode
  N14: HCSR04.TRIG, ARDUINO_MICRO.D7
  N15: HCSR04.ECHO, ARDUINO_MICRO.D6_PWM/A7
  N16: LIPO_5V_1A.+, BUTTON.leg1
  N17: ARDUINO_MICRO.A5, POT_RIGHT.S

notes:
  Wheel-bot, Initial version. https://github.com/ev0lutional/wheel-bot, 000

custom parts:
  Adafruit PCA9685 PWM/Servo Breakout: Using only two pins, control 16 free-running PWM outputs! I2C-controlled PWM driver with a built in clock. Unlike the TLC5940 family, you do not need to continuously send it signal tying up your microcontroller, its completely free running! 5V compliant, which means you can control it from a 3.3V microcontroller and still safely drive up to 6V outputs (this is good for when you want to control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
  HC-SR04 Ultrasonic Distance Sensor: The HC-SR04 is an ultrasonic distance sensor. It is capable of providing measurement for ranges of 2cm to 400cm. The module operates at 5V.
  Arduino Micro (Rev3): The Arduino Micro is a microcontroller board based on the ATmega32u4 (datasheet), developed in conjunction with Adafruit. It has 20 digital input/output pins (of which 7 can be used as PWM outputs and 12 as analog inputs), a 16 MHz crystal oscillator, a micro USB connection, an ICSP header, and a reset button. It contains everything needed to support the microcontroller; simply connect it to a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
